# Fritzing sketch asg1 (saved by Fritzing 0.9.3b)
breadboards: 1

parts:
  Esp32-cam1 = ESP32-Cam
  Part1 = HC-SR501 Body Sensor Module
  OLED1 = SSD1306 0.96in 128x64 I2C Monochrome OLED Display
  Part3 = USB converter CP2102

nets:
  5V: Esp32-cam1.5V, Part3.+5V
  GND: Esp32-cam1.GND, Esp32-cam1.GPIO_0, Part1.GND, OLED1.GND, Part3.GND
  N1: Esp32-cam1.GPIO_13, Part1.OUT
  N2: Esp32-cam1.GPIO_15, OLED1.SDA
  N3: Esp32-cam1.GPIO_14, OLED1.SCL
  VCC: Esp32-cam1.3.3V, Part1.VCC, OLED1.VCC
  N4: Esp32-cam1.RX/GPIO_3, Part3.TXO
  N5: Esp32-cam1.TX/GPIO_1, Part3.RXI

custom parts:
  HC-SR501 Body Sensor Module: Pyroelectric Infrared PIR Motion Sensor Detector Module
